// Logisim project ISA.circ as structural Verilog
module main (
  output [31:0] RSLT
);

  wire button_1_out, clk, clk_out, if_imm, ifBranch, ifJalr, ifJump, ldEN, mdctrl_1_c1, mdctrl_1_we, mux_imm,
       or_1_out, stop, wEN, wreg;
  wire [1:0] op;
  wire [2:0] op_ula;
  wire [4:0] rdaddr, rs1addr, rs2addr;
  wire [7:0] adder_2_out, mdctrl_1_a, multiplexer_1_out, multiplexer_2_out, PC_1, PC_q;
  wire [23:0] MI_data;
  wire [31:0] bit_extender_1_out, breg_1_rs2, imm, immctrl_1_seg_valor, mdctrl_1_d, multiplexer_4_out, RD,
       rs1, rs2, W;

  Multiplexer #(.width(8)) multiplexer_1 (
    .in0(multiplexer_2_out), .in1(rs1[7:0]), .out(multiplexer_1_out), .sel(ifJalr));
  Register PC (.D(multiplexer_1_out), .en(1'b1), .clk(clk), .Q(PC_q), .clr(button_1_out));
  Button button_1 (.out(button_1_out));
  Adder adder_1 (.a(PC_q), .b(8'h1), .out(PC_1));  // open: cin, cout
  Multiplexer #(.width(8)) multiplexer_2 (.in0(PC_1), .in1(adder_2_out), .out(multiplexer_2_out), .sel(or_1_out));
  or or_1 (or_1_out, ifJump, mux_imm);
  Adder adder_2 (.a(PC_q), .b(imm[7:0]), .out(adder_2_out));  // open: cin, cout
  Clock u_clk (.out(clk_out));
  ROM #(.dataWidth(24)) MI (.addr(PC_q), .data({MI_data[23:20], rdaddr, rs1addr, rs2addr, MI_data[4:0]}));
  and and_1 (clk, ~stop, clk_out);  // AND_Gate
  assign bit_extender_1_out = {{24{PC_1[7]}}, PC_1};  // Bit_Extender bit_extender_1
  Multiplexer #(.width(32)) multiplexer_3 (.in0(multiplexer_4_out), .in1(bit_extender_1_out), .out(RD), .sel(ifJump));
  UC uc_1 (
    .opcode(MI_data[23:20]), .op_branch(op), .stop(stop), .op_ula(op_ula), .ldEn(ldEN), .wEn(wEN),
    .ifBranch(ifBranch), .ifJump(ifJump), .if_imm(if_imm), .wReg(wreg), .ifJalr(ifJalr));
  Multiplexer #(.width(32)) multiplexer_4 (.in0(RSLT), .in1(W), .out(multiplexer_4_out), .sel(ldEN));
  BReg breg_1 (
    .rdAddr(rdaddr), .rs2Addr(rs2addr), .rs1Addr(rs1addr), .rd(RD), .clk(clk), .wReg(wreg), .rs2(breg_1_rs2),
    .rs1(rs1));
  gera_imm gera_imm_1 (.bits(MI_data[4:0]), .imm(imm));
  RAM #(.dataWidth(32), .enables("line")) ram_1 (
    .addr(mdctrl_1_a), .we(mdctrl_1_we), .clk(mdctrl_1_c1), .din(mdctrl_1_d), .dout(W));
  mdCTRL mdctrl_1 (
    .clk(clk), .rs2(rs2), .imm(imm), .wEN(wEN), .rs1Addr(rs1addr), .A(mdctrl_1_a), .WE(mdctrl_1_we),
    .C1(mdctrl_1_c1), .D(mdctrl_1_d));
  branch branch_1 (.rs1(rs1), .op(op), .rs2(breg_1_rs2), .ifbranch(ifBranch), .res(mux_imm));
  immCTRL immctrl_1 (.rs2(breg_1_rs2), .imm(imm), .if_imm(if_imm), .seg_valor(immctrl_1_seg_valor));
  ULA ula_1 (.rs1(rs1), .seg_valor(immctrl_1_seg_valor), .op_ula(op_ula), .saida(RSLT));

  // Notes on the sheet:
  //   contents of MI (hex, n*v repeats v):
  //   a08003 1283e8 f00000 128009 b00400
  //   MI
  //   MD
endmodule

module BReg (
  input  [31:0] rd,
  input  [4:0] rs2Addr,
  input  wReg,
  input  [4:0] rdAddr,
  input  clk,
  input  [4:0] rs1Addr,
  output [31:0] rs2,
  output [31:0] rs1
);

  wire X0wReg, X1wReg, X2wReg, X3wReg, X4wReg, X5wReg, X6wReg, X7wReg, X8wReg, X9wReg, X10wReg, X11wReg,
       X12wReg, X13wReg, X14wReg, X15wReg, X16wReg, X17wReg, X18wReg, X19wReg, X20wReg, X21wReg, X22wReg,
       X23wReg, X24wReg, X25wReg, X26wReg, X27wReg, X28wReg, X29wReg, X30wReg, X31wReg;
  wire [31:0] X1q, X2q, X3q, X4q, X5q, X6q, X7q, X8q, X9q, X10q, X11q, X12q, X13q, X14q, X15q, X16q, X17q,
       X18q, X19q, X20q, X21q, X22q, X23q, X24q, X25q, X26q, X27q, X28q, X29q, X30q, X31q;

  Demultiplexer #(.select(5)) demultiplexer_1 (
    .out0(X0wReg), .out1(X1wReg), .out2(X2wReg), .out3(X3wReg), .out4(X4wReg), .out5(X5wReg), .out6(X6wReg),
    .out7(X7wReg), .out8(X8wReg), .out9(X9wReg), .out10(X10wReg), .out11(X11wReg), .out12(X12wReg),
    .out13(X13wReg), .out14(X14wReg), .out15(X15wReg), .out16(X16wReg), .out17(X17wReg), .out18(X18wReg),
    .out19(X19wReg), .out20(X20wReg), .out21(X21wReg), .out22(X22wReg), .out23(X23wReg), .out24(X24wReg),
    .out25(X25wReg), .out26(X26wReg), .out27(X27wReg), .out28(X28wReg), .out29(X29wReg), .out30(X30wReg),
    .out31(X31wReg), .in(wReg), .sel(rdAddr));
  Register #(.width(32)) X4 (.D(rd), .en(X4wReg), .clk(clk), .Q(X4q));  // open: clr
  Register #(.width(32)) X8 (.D(rd), .en(X8wReg), .clk(clk), .Q(X8q));  // open: clr
  Register #(.width(32)) X12 (.D(rd), .en(X12wReg), .clk(clk), .Q(X12q));  // open: clr
  Register #(.width(32)) X1 (.D(rd), .en(X1wReg), .clk(clk), .Q(X1q));  // open: clr
  Register #(.width(32)) X5 (.D(rd), .en(X5wReg), .clk(clk), .Q(X5q));  // open: clr
  Register #(.width(32)) X9 (.D(rd), .en(X9wReg), .clk(clk), .Q(X9q));  // open: clr
  Register #(.width(32)) X13 (.D(rd), .en(X13wReg), .clk(clk), .Q(X13q));  // open: clr
  Register #(.width(32)) X2 (.D(rd), .en(X2wReg), .clk(clk), .Q(X2q));  // open: clr
  Register #(.width(32)) X6 (.D(rd), .en(X6wReg), .clk(clk), .Q(X6q));  // open: clr
  Register #(.width(32)) X10 (.D(rd), .en(X10wReg), .clk(clk), .Q(X10q));  // open: clr
  Register #(.width(32)) X14 (.D(rd), .en(X14wReg), .clk(clk), .Q(X14q));  // open: clr
  Register #(.width(32)) X3 (.D(rd), .en(X3wReg), .clk(clk), .Q(X3q));  // open: clr
  Register #(.width(32)) X7 (.D(rd), .en(X7wReg), .clk(clk), .Q(X7q));  // open: clr
  Register #(.width(32)) X11 (.D(rd), .en(X11wReg), .clk(clk), .Q(X11q));  // open: clr
  Register #(.width(32)) X15 (.D(rd), .en(X15wReg), .clk(clk), .Q(X15q));  // open: clr
  Register #(.width(32)) X16 (.D(rd), .en(X16wReg), .clk(clk), .Q(X16q));  // open: clr
  Register #(.width(32)) X20 (.D(rd), .en(X20wReg), .clk(clk), .Q(X20q));  // open: clr
  Register #(.width(32)) X24 (.D(rd), .en(X24wReg), .clk(clk), .Q(X24q));  // open: clr
  Register #(.width(32)) X28 (.D(rd), .en(X28wReg), .clk(clk), .Q(X28q));  // open: clr
  Register #(.width(32)) X17 (.D(rd), .en(X17wReg), .clk(clk), .Q(X17q));  // open: clr
  Register #(.width(32)) X21 (.D(rd), .en(X21wReg), .clk(clk), .Q(X21q));  // open: clr
  Register #(.width(32)) X25 (.D(rd), .en(X25wReg), .clk(clk), .Q(X25q));  // open: clr
  Register #(.width(32)) X29 (.D(rd), .en(X29wReg), .clk(clk), .Q(X29q));  // open: clr
  Register #(.width(32)) X18 (.D(rd), .en(X18wReg), .clk(clk), .Q(X18q));  // open: clr
  Register #(.width(32)) X22 (.D(rd), .en(X22wReg), .clk(clk), .Q(X22q));  // open: clr
  Register #(.width(32)) X26 (.D(rd), .en(X26wReg), .clk(clk), .Q(X26q));  // open: clr
  Register #(.width(32)) X30 (.D(rd), .en(X30wReg), .clk(clk), .Q(X30q));  // open: clr
  Register #(.width(32)) X19 (.D(rd), .en(X19wReg), .clk(clk), .Q(X19q));  // open: clr
  Register #(.width(32)) X23 (.D(rd), .en(X23wReg), .clk(clk), .Q(X23q));  // open: clr
  Register #(.width(32)) X27 (.D(rd), .en(X27wReg), .clk(clk), .Q(X27q));  // open: clr
  Register #(.width(32)) X31 (.D(rd), .en(X31wReg), .clk(clk), .Q(X31q));  // open: clr
  Multiplexer #(.select(5), .width(32)) multiplexer_1 (
    .in0({32{1'b0}}), .in1(X1q), .in2(X2q), .in3(X3q), .in4(X4q), .in5(X5q), .in6(X6q), .in7(X7q), .in8(X8q),
    .in9(X9q), .in10(X10q), .in11(X11q), .in12(X12q), .in13(X13q), .in14(X14q), .in15(X15q), .in16(X16q),
    .in17(X17q), .in18(X18q), .in19(X19q), .in20(X20q), .in21(X21q), .in22(X22q), .in23(X23q), .in24(X24q),
    .in25(X25q), .in26(X26q), .in27(X27q), .in28(X28q), .in29(X29q), .in30(X30q), .in31(X31q), .out(rs2),
    .sel(rs2Addr));
  Multiplexer #(.select(5), .width(32)) multiplexer_2 (
    .in0({32{1'b0}}), .in1(X1q), .in2(X2q), .in3(X3q), .in4(X4q), .in5(X5q), .in6(X6q), .in7(X7q), .in8(X8q),
    .in9(X9q), .in10(X10q), .in11(X11q), .in12(X12q), .in13(X13q), .in14(X14q), .in15(X15q), .in16(X16q),
    .in17(X17q), .in18(X18q), .in19(X19q), .in20(X20q), .in21(X21q), .in22(X22q), .in23(X23q), .in24(X24q),
    .in25(X25q), .in26(X26q), .in27(X27q), .in28(X28q), .in29(X29q), .in30(X30q), .in31(X31q), .out(rs1),
    .sel(rs1Addr));

  // Other names for the same wires on the sheet: tclock = clk
endmodule

module ULA (
  input  [31:0] rs1,
  input  [31:0] seg_valor,
  input  [2:0] op_ula,
  output [31:0] saida
);

  wire [31:0] adder_1_out, and_1_out, multiplier_1_out, negator_1_out, or_1_out, shifter_1_out,
       shifter_2_out, subtractor_1_out;

  Adder #(.width(32)) adder_1 (.a(rs1), .b(seg_valor), .out(adder_1_out));  // open: cin, cout
  Subtractor #(.width(32)) subtractor_1 (.a(rs1), .b(seg_valor), .out(subtractor_1_out));  // open: bin, bout
  Shifter #(.width(32)) shifter_1 (.in(rs1), .\dist (seg_valor[4:0]), .out(shifter_1_out));
  Shifter #(.shift("ar"), .width(32)) shifter_2 (.in(rs1), .\dist (seg_valor[4:0]), .out(shifter_2_out));
  Multiplier #(.width(32)) multiplier_1 (.a(rs1), .b(seg_valor), .out(multiplier_1_out));  // open: cin, cout
  assign and_1_out = rs1 & seg_valor;  // AND_Gate and_1, 32 bits wide
  assign or_1_out = rs1 | seg_valor;  // OR_Gate or_1, 32 bits wide
  Negator #(.width(32)) negator_1 (.in(rs1), .out(negator_1_out));
  Multiplexer #(.select(3), .width(32)) multiplexer_1 (
    .in0(adder_1_out), .in1(subtractor_1_out), .in2(shifter_1_out), .in3(shifter_2_out),
    .in4(multiplier_1_out), .in5(and_1_out), .in6(or_1_out), .in7(negator_1_out), .out(saida), .sel(op_ula));
endmodule

module gera_imm (
  input  [4:0] bits,
  output [31:0] imm
);

  assign imm = {{27{bits[4]}}, bits};  // Bit_Extender bit_extender_1
endmodule

module branch (
  input  [31:0] rs1,
  input  [1:0] op,
  input  [31:0] rs2,
  input  ifbranch,
  output res
);

  wire comparator_1_eq, comparator_1_gt, multiplexer_1_out, or_1_out;

  Comparator #(.width(32)) comparator_1 (.a(rs1), .b(rs2), .gt(comparator_1_gt), .eq(comparator_1_eq));  // open: lt
  or or_1 (or_1_out, comparator_1_gt, comparator_1_eq);
  Multiplexer #(.select(2)) multiplexer_1 (
    .in1(comparator_1_eq), .in2(or_1_out), .out(multiplexer_1_out), .sel(op));  // open: in0, in3
  and and_1 (res, multiplexer_1_out, ifbranch);
endmodule

module immCTRL (
  input  [31:0] rs2,
  input  [31:0] imm,
  input  if_imm,
  output [31:0] seg_valor
);

  Multiplexer #(.width(32)) multiplexer_1 (.in0(rs2), .in1(imm), .out(seg_valor), .sel(if_imm));
endmodule

module UC (
  input  [3:0] opcode,
  output [2:0] op_ula,
  output if_imm,
  output ldEn,
  output wEn,
  output [1:0] op_branch,
  output wReg,
  output stop,
  output ifJalr,
  output ifBranch,
  output ifJump
);

  wire add, addi, and_out, jal, mul, ngt, or_out, sll_out, srl_out, sub;

  and and_1 (add, ~opcode[3], ~opcode[2], ~opcode[1], ~opcode[0]);  // AND_Gate
  and and_2 (addi, ~opcode[3], ~opcode[2], ~opcode[1], opcode[0]);  // AND_Gate
  and and_3 (sub, ~opcode[3], ~opcode[2], opcode[1], ~opcode[0]);  // AND_Gate
  and and_4 (sll_out, ~opcode[3], ~opcode[2], opcode[1], opcode[0]);  // AND_Gate
  and and_5 (srl_out, ~opcode[3], opcode[2], ~opcode[1], ~opcode[0]);  // AND_Gate
  and and_6 (mul, ~opcode[3], opcode[2], ~opcode[1], opcode[0]);  // AND_Gate
  and and_7 (and_out, ~opcode[3], opcode[2], opcode[1], ~opcode[0]);  // AND_Gate
  and and_8 (or_out, ~opcode[3], opcode[2], opcode[1], opcode[0]);  // AND_Gate
  and and_9 (op_branch[0], opcode[3], ~opcode[2], ~opcode[1], ~opcode[0]);  // AND_Gate
  and and_10 (ngt, opcode[3], ~opcode[2], ~opcode[1], opcode[0]);  // AND_Gate
  and and_11 (jal, opcode[3], ~opcode[2], opcode[1], ~opcode[0]);  // AND_Gate
  and and_12 (ifJalr, opcode[3], ~opcode[2], opcode[1], opcode[0]);  // AND_Gate
  and and_13 (ldEn, opcode[3], opcode[2], ~opcode[1], ~opcode[0]);  // AND_Gate
  and and_14 (wEn, opcode[3], opcode[2], ~opcode[1], opcode[0]);  // AND_Gate
  and and_15 (op_branch[1], opcode[3], opcode[2], opcode[1], ~opcode[0]);  // AND_Gate
  and and_16 (stop, opcode[3], opcode[2], opcode[1], opcode[0]);
  or or_1 (ifBranch, op_branch[0], op_branch[1]);
  or or_2 (ifJump, jal, ifJalr);
  or or_3 (if_imm, addi, sll_out, srl_out);
  or or_4 (wReg, jal, ldEn, add, addi, sub, sll_out, mul, and_out, or_out, ngt, srl_out, ifJalr);
  or or_5 (op_ula[0], sub, srl_out, and_out, ngt);
  or or_6 (op_ula[1], sll_out, srl_out, or_out, ngt);
  or or_7 (op_ula[2], mul, and_out, or_out, ngt);

  // Other names for the same wires on the sheet: jalr = ifJalr; ld = ldEn; beq = op_branch[0]; bge = op_branch[1];
  //   ula0 = op_ula[0]; ula1 = op_ula[1]; ula2 = op_ula[2]; bit0 = opcode[0]; bit1 = opcode[1]; bit2 = opcode[2];
  //   bit3 = opcode[3]; st = wEn

  // Notes on the sheet:
  //   bits da ULA
endmodule

module mdCTRL (
  input  [4:0] rs1Addr,
  input  [31:0] imm,
  input  wEN,
  input  clk,
  input  [31:0] rs2,
  output [7:0] A,
  output WE,
  output C1,
  output [31:0] D
);

  wire [7:0] adder_1_out, bit_extender_1_out, bit_extender_2_out;

  assign bit_extender_1_out = {{3{rs1Addr[4]}}, rs1Addr};  // Bit_Extender bit_extender_1
  Adder adder_1 (.a(bit_extender_1_out), .b(imm[7:0]), .out(adder_1_out));  // open: cin, cout
  assign bit_extender_2_out = {{7{wEN}}, wEN};  // Bit_Extender bit_extender_2
  assign A = adder_1_out & bit_extender_2_out;  // AND_Gate and_1, 8 bits wide

  assign C1 = clk;
  assign D = rs2;
  assign WE = wEN;
endmodule

module d (
);

  BReg breg_1 ();  // open: rdAddr, rs2Addr, rs1Addr, rd, clk, wReg, rs2, rs1
endmodule
